# Fritzing sketch morse (saved by Fritzing 0.9.2b)
breadboards: 1

parts:
  Nano = Arduino Nano (Rev3.0)
  LED1 = LED - 5mm [color="Red (633nm)" package="5 mm [THT]"]
  Speaker = Piezo Speaker

nets:
  N1: Nano.GND, LED1.cathode, Speaker.pin1
  N2: Nano.D9, LED1.anode
  N3: Nano.D10, Speaker.pin2
